// Logisim project Basic_Gates_Logisim.circ as structural Verilog: 1 circuit
module Main (
);

  wire A_p1, and_1_p2, B_p1, nand_1_p1, nor_1_p1, not_1_p1, or_1_p2, xnor_1_p1, xor_1_p1;

  // Pin A: pin names not known; wires that end beside it: A_p1
  // Pin B: pin names not known; wires that end beside it: B_p1
  // AND_Gate and_1: pin names not known; wires that end beside it: A_p1, and_1_p2
  // OR_Gate or_1: pin names not known; wires that end beside it: B_p1, or_1_p2
  // NOT_Gate not_1: pin names not known; wires that end beside it: not_1_p1
  // NAND_Gate nand_1: pin names not known; wires that end beside it: nand_1_p1
  // NOR_Gate nor_1: pin names not known; wires that end beside it: nor_1_p1
  // XOR_Gate xor_1: pin names not known; wires that end beside it: xor_1_p1
  // XNOR_Gate xnor_1: pin names not known; wires that end beside it: xnor_1_p1
  // LED AND_2: pin names not known; wires that end beside it: and_1_p2
  // LED OR_2: pin names not known; wires that end beside it: or_1_p2
  // LED NOT_A: pin names not known; wires that end beside it: not_1_p1
  // LED NAND_2: pin names not known; wires that end beside it: nand_1_p1
  // LED NOR_2: pin names not known; wires that end beside it: nor_1_p1
  // LED XOR_2: pin names not known; wires that end beside it: xor_1_p1
  // LED XNOR_2: pin names not known; wires that end beside it: xnor_1_p1
endmodule
