// Logisim project Half_Adder_Logisim.circ as structural Verilog: 1 circuit
module Main (
);

  wire A_p1, and_1_p2, B_p1, xor_1_p2;

  // Pin A: pin names not known; wires that end beside it: A_p1
  // Pin B: pin names not known; wires that end beside it: B_p1
  // XOR_Gate xor_1: pin names not known; wires that end beside it: A_p1, xor_1_p2
  // AND_Gate and_1: pin names not known; wires that end beside it: B_p1, and_1_p2
  // LED Sum__S: pin names not known; wires that end beside it: xor_1_p2
  // LED Carry__C: pin names not known; wires that end beside it: and_1_p2
endmodule
