// Logisim project Tri_State_Buffer_74125_Logisim.circ as structural Verilog: 1 circuit
module Main (
);

  wire A_p1, and_1_p3, controlled_switch_1_p2, G_prime_p1, not_1_p2;

  // Pin A: pin names not known; wires that end beside it: A_p1
  // Pin G_prime: pin names not known; wires that end beside it: G_prime_p1
  // NOT_Gate not_1: pin names not known; wires that end beside it: G_prime_p1, not_1_p2
  // AND_Gate and_1: pin names not known; wires that end beside it: A_p1, not_1_p2, and_1_p3
  // Controlled_Switch controlled_switch_1: pin names not known; wires that end beside it: and_1_p3, controlled_switch_1_p2
  // LED Y: pin names not known; wires that end beside it: controlled_switch_1_p2
endmodule
