// Logisim project Universal_Gates_Logisim.circ as structural Verilog: 1 circuit
module Main (
);

  wire A_p1, B_p1, nand_1_p2, nand_2_p2, nand_3_p1, nand_4_p1, nor_1_p1, nor_2_p1, nor_3_p1, nor_4_p1;

  // Pin A: pin names not known; wires that end beside it: A_p1
  // Pin B: pin names not known; wires that end beside it: B_p1
  // NAND_Gate nand_1: pin names not known; wires that end beside it: A_p1, nand_1_p2
  // NAND_Gate nand_2: pin names not known; wires that end beside it: B_p1, nand_2_p2
  // NAND_Gate nand_3: pin names not known; wires that end beside it: nand_3_p1
  // NAND_Gate nand_4: pin names not known; wires that end beside it: nand_4_p1
  // LED NAND_1: pin names not known; wires that end beside it: nand_1_p2
  // LED NAND_2: pin names not known; wires that end beside it: nand_2_p2
  // LED NAND_3: pin names not known; wires that end beside it: nand_3_p1
  // LED NAND_4: pin names not known; wires that end beside it: nand_4_p1
  // NOR_Gate nor_1: pin names not known; wires that end beside it: nor_1_p1
  // NOR_Gate nor_2: pin names not known; wires that end beside it: nor_2_p1
  // NOR_Gate nor_3: pin names not known; wires that end beside it: nor_3_p1
  // NOR_Gate nor_4: pin names not known; wires that end beside it: nor_4_p1
  // LED NOR_1: pin names not known; wires that end beside it: nor_1_p1
  // LED NOR_2: pin names not known; wires that end beside it: nor_2_p1
  // LED NOR_3: pin names not known; wires that end beside it: nor_3_p1
  // LED NOR_4: pin names not known; wires that end beside it: nor_4_p1
endmodule
